// Logisim project ALU_Project.circ as structural Verilog: 3 circuits, main circuit main
module main (
  input  CIN,
  input  [3:0] A,
  input  [3:0] B,
  output [3:0] Y,
  output Overflow,
  output COUT
);

  wire adder_1_cout, adder_2_cout, adder_3_cout;

  Adder #(.width(1)) adder_1 (.a(A[0]), .b(B[0]), .out(Y[0]), .cin(CIN), .cout(adder_1_cout));
  Adder #(.width(1)) adder_2 (.a(A[1]), .b(B[1]), .out(Y[1]), .cin(adder_1_cout), .cout(adder_2_cout));
  Adder #(.width(1)) adder_3 (.a(A[2]), .b(B[2]), .out(Y[2]), .cin(adder_2_cout), .cout(adder_3_cout));
  Adder #(.width(1)) adder_4 (.a(A[3]), .b(B[3]), .out(Y[3]), .cin(adder_3_cout), .cout(COUT));
  xor xor_1 (Overflow, adder_3_cout, COUT);
endmodule

module LU (
  input  [3:0] A,
  input  [3:0] B,
  input  f2,
  input  f0,
  output [3:0] Y
);

  wire [3:0] and_1_out, or_1_out, xor_1_out;

  assign and_1_out = A & B;  // AND_Gate and_1, 4 bits wide
  assign or_1_out = A | B;  // OR_Gate or_1, 4 bits wide
  assign xor_1_out = A ^ B;  // XOR_Gate xor_1, 4 bits wide
  Multiplexer #(.select(2), .width(4)) multiplexer_1 (
    .in0(and_1_out), .in1(or_1_out), .in2(xor_1_out), .in3(B), .out(Y), .sel({f2, f0}));
endmodule

module ALU (
  input  [3:0] in_1,
  input  [3:0] in_2,
  input  [3:0] in_3,
  output v,
  output c,
  output z,
  output out_7,
  output [3:0] y
);

  wire [3:0] lu_1_y, main_1_y, multiplexer_1_out, multiplexer_2_out, not_1_out, not_2_out;

  assign not_1_out = ~in_1;  // NOT_Gate not_1, 4 bits wide
  assign not_2_out = ~in_2;  // NOT_Gate not_2, 4 bits wide
  Multiplexer #(.width(4)) multiplexer_1 (.in0(in_1), .in1(not_1_out), .out(multiplexer_1_out), .sel(in_3[0]));
  Multiplexer #(.width(4)) multiplexer_2 (.in0(in_2), .in1(not_2_out), .out(multiplexer_2_out), .sel(in_3[1]));
  main main_1 (.CIN(in_3[2]), .A(multiplexer_1_out), .B(multiplexer_2_out), .Y(main_1_y), .Overflow(v), .COUT(c));
  Multiplexer #(.width(4)) multiplexer_3 (.in0(main_1_y), .in1(lu_1_y), .out({out_7, y[2:0]}), .sel(in_3[3]));
  LU lu_1 (.A(in_1), .B(multiplexer_2_out), .f2(in_3[2]), .f0(in_3[0]), .Y(lu_1_y));
  nor nor_1 (z, y[0], y[1], y[2], out_7);

  assign y[3] = out_7;
endmodule
